# Fritzing sketch breadboard (saved by Fritzing 0.9.4)
breadboards: 1

parts:
  U1 = NodeMCU V1.0
  LED1 = LED - 3mm [color="Green (570nm)" package="3 mm [THT]"]
  LED2 = LED - 3mm [color="Yellow (595nm)" package="3 mm [THT]"]
  LED3 = LED - 3mm [color="Red (633nm)" package="3 mm [THT]"]
  LED4 = LED - 3mm [color="Blue (430nm)" package="3 mm [THT]"]
  R1 = Resistor [tolerance=±5% resistance=330 package=THT]
  R2 = Resistor [tolerance=±5% resistance=330 package=THT]
  R3 = Resistor [tolerance=±5% resistance=330 package=THT]
  R4 = Resistor [tolerance=±5% resistance=330 package=THT]

nets:
  N1: U1.D1, R3.Pin_0
  N2: U1.GND, LED1.cathode, LED2.cathode, LED3.cathode, LED4.cathode
  N3: U1.D5, R4.Pin_0
  N4: U1.D6, R2.Pin_0
  N5: U1.D7, R1.Pin_0
  N6: LED1.anode, R3.Pin_1
  N7: LED2.anode, R4.Pin_1
  N8: LED3.anode, R2.Pin_1
  N9: LED4.anode, R1.Pin_1

custom parts:
  NodeMCU V1.0: ESP8266 based NodeMCU
